# Fritzing sketch prototype3Layout (saved by Fritzing 0.9.1b)
breadboards: 2

parts:
  Part1 = Arduino Mega 2560 (Rev3)
  IC1 = H-Bridge [package=THT]
  IC2 = H-Bridge [package=THT]
  IC3 = H-Bridge [package=THT]
  IC4 = H-Bridge [package=THT]
  IC5 = H-Bridge [package=THT]
  BAT1 = BC9VPC [package=bc9vpc]

nets:
  GND1: Part1.GND, IC3.GND1, IC3.GND2, IC4.GND1, IC4.GND2
  N1: Part1.D10_PWM, IC3.3_4EN
  N2: Part1.D9_PWM, IC4.1_2EN
  N3: Part1.D8_PWM, IC3.1_2EN
  N4: Part1.5V, IC1.VCC1, IC2.VCC1, IC5.VCC1
  N5: Part1.D2_PWM, IC1.1_2EN
  N6: Part1.D3_PWM, IC2.1_2EN
  N7: Part1.D4_PWM, IC5.1_2EN
  N8: Part1.D5_PWM, IC5.3_4EN
  N9: Part1.D6_PWM, IC2.3_4EN
  N10: Part1.D7_PWM, IC1.3_4EN
  GND1_2: IC1.GND1, IC1.GND2, IC2.GND1, IC2.GND2, IC5.GND1, IC5.GND2, BAT1.V-
  N11: IC1.VCC2, IC2.VCC2, IC3.VCC2, IC4.VCC2, IC5.VCC2, BAT1.V+
  GND3: IC1.GND3, IC1.GND4, IC2.GND3, IC2.GND4, IC5.GND3, IC5.GND4
  GND3_2: IC3.GND3, IC3.GND4, IC4.GND3, IC4.GND4
  N12: IC3.VCC1, IC4.VCC1
